# Fritzing sketch serial display (saved by Fritzing 0.9.2b)
circuit board: 8.46667cm x 5.64444cm
breadboards: 1

parts:
  Part1 = Arduino Leonardo (Rev3b)
  LCD1 = LCD screen
  R1 = Resistor [tolerance=±5% resistance=2.2k package=THT]
  R2 = Resistor [tolerance=±5% resistance=2.2k package=THT]
  S1 = Pushbutton [package="[THT]"]
  S2 = Pushbutton [package="[THT]"]
  R3 = Resistor [tolerance=±5% resistance=1k package=THT]

nets:
  N1: Part1.D0/RX, R1.Pin_1, S1.Pin_3
  N2: Part1.D1/TX, R2.Pin_1, S2.Pin_3, S2.Pin_4
  N3: Part1.D3_PWM/SCL, Part1.SCL, LCD1.E
  N4: Part1.D4/A6, LCD1.DB5
  N5: Part1.D5_PWM, LCD1.DB4
  N6: Part1.D6_PWM/A7, LCD1.DB7
  N7: Part1.D7, LCD1.DB6
  5V: Part1.5V, LCD1.VDD, R1.Pin_0, R2.Pin_0, R3.Pin_0
  GND: Part1.GND, LCD1.VSS, LCD1.R/W, LCD1.LED-, S1.Pin_1, S2.Pin_1
  N8: Part1.A0, LCD1.V0
  N9: Part1.SDA, LCD1.RS
  N10: LCD1.LED+, R3.Pin_1
